# Fritzing sketch sketch (saved by Fritzing 0.9.3b)
circuit board: 5.69788cm x 7.12842cm
perfboards: 1

parts:
  R1 = Resistor [tolerance=±5% resistance=330 package=THT]
  Part1 = Arduino Nano (Rev3.0)
  J1 = Piezo Speaker
  LED1 = LED - 5mm [color="Red (633nm)" package="5 mm [THT]"]
  Fan2 = Header 4 [package=molex-1x4_lock]
  Fan1 = Header 4 [package=molex-1x4_lock]
  Fan3 = Header 4 [package=molex-1x4_lock]
  Fan4 = Header 4 [package=molex-1x4_lock]
  Fan5 = Header 4 [package=molex-1x4_lock]
  Power = Header 3 [package=molex-1x3_lock]
  Button = Header 2 [package=molex-1x2_lock]
  SSD1306 = Header 4 [package=molex-1x4_lock]
  Sensor2 = Header 2 [package=molex-1x2_lock]
  Sensor1 = Header 2 [package=molex-1x2_lock]
  R2 = Resistor [tolerance=±5% resistance=10k package=THT]
  R3 = Resistor [tolerance=±5% resistance=10k package=THT]
  R5 = Resistor [tolerance=±5% resistance=10k package=THT]
  R6 = Resistor [tolerance=±5% resistance=10k package=THT]

nets:
  N1: R1.Pin_0, LED1.anode
  N2: R1.Pin_1, Part1.D12/MISO
  N3: Part1.D0/RX, Button.2
  N4: Part1.GND, Power.2, R2.Pin_1, R3.Pin_1
  N5: Part1.D2, Fan1.3, R6.Pin_1
  N6: Part1.D3, Fan2.3, R5.Pin_1
  N7: Part1.D5, Fan5.4
  N8: Part1.D6, Fan4.4
  N9: Part1.D8, J1.pin1
  N10: Part1.D9, Fan3.4
  N11: Part1.D10, Fan2.4
  N12: Part1.D11/MOSI, Fan1.4
  5V: Part1.VIN, Power.3
  N13: Part1.5V, Sensor2.2, Sensor1.1, R5.Pin_0, R6.Pin_0
  N14: Part1.A5, SSD1306.3
  N15: Part1.A4, SSD1306.4
  N16: Part1.A3, Sensor2.1, R2.Pin_0
  N17: Part1.A2, Sensor1.2, R3.Pin_0
  N18: Part1.3V3, SSD1306.1
  GND: J1.pin2, LED1.cathode, Fan2.1, Fan1.1, Fan3.1, Fan4.1, Fan5.1, Button.1, SSD1306.2
  N19: Fan2.2, Fan1.2, Fan3.2, Fan4.2, Fan5.2, Power.1

notes:
  Purple: wires
  <----------------------- buzzer slot here (pink)
  See breadboard section for PCB
